// Logisim project seven_segment_display.circ as structural Verilog: 1 circuit, main circuit main
module main (
  input  b0,
  input  b1,
  input  b2,
  input  b3
);

  wire a_out, and_1_out, and_2_out, and_3_out, and_4_out, b_out, not_1_out, not_2_out, not_3_out, or_1_out;

  not not_1 (not_1_out, b0);
  not not_2 (not_2_out, b1);
  not not_3 (not_3_out, b2);
  and and_1 (and_1_out, b0, b2);
  and and_2 (and_2_out, not_1_out, not_3_out);
  or a (a_out, and_1_out, and_2_out, b1, b3);
  and and_3 (and_3_out, b1, b0);
  and and_4 (and_4_out, not_2_out, not_1_out);
  or b (b_out, and_3_out, and_4_out, not_3_out);
  or or_1 (or_1_out, not_2_out, b0, b2);
  _7_Segment_Display u_7_segment_display_1 (.a(a_out), .b(b_out), .c(or_1_out));  // open: g, f, e, d, dp
endmodule
